# Fritzing sketch catbot (saved by Fritzing 0.8.7b)
breadboards: 1

parts:
  LED1 = LED - 5mm [color="Red (633nm)" package="5 mm [THT]"]
  R1 = Resistor [tolerance=±5% resistance=220 package=THT]
  J1 = Basic Servo
  J2 = Basic Servo
  Q1 = NPN-Transistor [package="TO92 [THT]"]
  LED2 = LED - 5mm [color="Red (633nm)" package="5 mm [THT]"]
  R2 = Resistor [tolerance=±5% resistance=560 package="0603 [SMD]"]
  Composants1 = Arduino Uno (Rev3)

nets:
  GND: LED1.cathode, J1.gnd, J2.gnd, Q1.B, Composants1.GND
  N1: LED1.anode, R1.Pin_1
  N2: R1.Pin_0, Composants1.D13/SCK
  VCC: J1.vcc, J2.vcc, LED2.anode, Composants1.5V
  N3: J1.pulse, Composants1.D9_PWM
  N4: J2.pulse, Composants1.D10_PWM/SS
  N5: Q1.E, R2.Pin_1
  N6: Q1.C, LED2.cathode
  N7: R2.Pin_0, Composants1.D12/MISO
