# Fritzing sketch catbot2 (saved by Fritzing 0.8.7b)
breadboards: 1

parts:
  LED1 = LED - 5mm [color="Red (633nm)" package="5 mm [THT]"]
  R1 = Resistor [tolerance=±5% resistance=220 package=THT]
  J1 = Basic Servo
  J2 = Basic Servo
  LED2 = LED - 5mm [color="Red (633nm)" package="5 mm [THT]"]
  R2 = Resistor [tolerance=±5% resistance=560 package="0603 [SMD]"]
  Part1 = Iteaduino UNO
  Q1 = NPN-Transistor [package="TO92 [THT]"]

nets:
  N1: LED1.cathode, Q1.B
  N2: LED1.anode, R1.Pin_1
  N3: J1.gnd, Part1.GND#167
  N4: J1.vcc, Part1.VCC#142
  N5: J2.gnd, Part1.GND#165
  N6: J2.vcc, Part1.VCC#140
  N7: J2.pulse, Part1.D11
  N8: LED2.cathode, Q1.C
  N9: R2.Pin_1, Q1.E

custom parts:
  Iteaduino UNO: Breakout board Platform Based On Arduino by Iteadstudio Principal features : Electronic Brick Ports 3.3V or 5V power supply The official support forum: support@iteadstudio.com
